# Fritzing sketch rfidmusicbox (saved by Fritzing 0.9.3b)
breadboards: 1

parts:
  U1 = ESP32S-HiLetgo [part_number=nodemcu-32s]
  DFPlayer_Mini1 = DFPlayer MINI [package="DIP (Dual Inline) [THT]"]
  R1 = Resistor [tolerance=±5% resistance=1k package=THT]
  SP1 = SPEAKER [package=pcb_mount_speaker]
  Part1 = RFID-RC522-v2
  S1 = Round Pushbutton
  S2 = Round Pushbutton
  S3 = Round Pushbutton
  R2 = Resistor [tolerance=±5% resistance=10k package=THT]
  R3 = Resistor [tolerance=±5% resistance=10k package=THT]
  R4 = Resistor [tolerance=±5% resistance=10k package=THT]

nets:
  VCC: U1.3.3, DFPlayer_Mini1.VCC, Part1.3.3V, S1.leg1, S2.leg1, S3.leg1
  N1: U1.GPIO34, S3.leg0, R4.Pin_1
  N2: U1.GPIO35, S2.leg0, R3.Pin_1
  N3: U1.GPIO32, S1.leg0, R2.Pin_1
  N4: U1.GPIO33, Part1.RST
  N5: U1.GND, R3.Pin_0, R4.Pin_0
  N6: U1.GPIO16, DFPlayer_Mini1.RX
  N7: U1.GPIO17, R1.Pin_0
  N8: U1.GPIO5, Part1.SDA
  N9: U1.GPIO18, Part1.SCK
  N10: U1.GPIO19, Part1.MISO
  N11: U1.GPIO23, Part1.MOSI
  N12: DFPlayer_Mini1.TX, R1.Pin_1
  N13: DFPlayer_Mini1.SPK1, SP1.+
  GND: DFPlayer_Mini1.GND, Part1.GND, R2.Pin_0
  N14: DFPlayer_Mini1.SPK2, SP1.-

custom parts:
  ESP32S-HiLetgo: HiLetgo ESP-WROOM-32 ESP32 ESP-32S Development Board 2.4GHz Dual-Mode WiFi + Bluetooth Dual Cores Microcontroller The ESP32 integrated with Antenna switches, RF Balun, power amplifiers, low-noise amplifiers, filters, and management modules, and the entire solution occupies the least area of PCB. 2.4 GHz Wi-Fi plus Bluetooth dual-mode chip, with TSMC Ultra-low power consumption 40nm technology,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
  DFPlayer MINI: MP3 module by DFRobot.com for playing Music from an SD-Card. Supports WAV and MP3 files.
  RFID-RC522-v2: A simple China made RFID-RC522 Reader; do check the pin labels, as this is a MFRC522 based clone.
